# Fritzing sketch AirQ (saved by Fritzing 0.9.4)
circuit board: 4.67811cm x 3.37928cm

parts:
  Q1 = NPN-Transistor [package="TO92 [THT]"]
  Q2 = NPN-Transistor [package="TO92 [THT]"]
  Q3 = NPN-Transistor [package="TO92 [THT]"]
  Q4 = NPN-Transistor [package="TO92 [THT]"]
  C1 = Electrolytic Capacitor [capacitance=1µF package="100 mil [THT, electrolytic]"]
  YELLOW = Super Flux LED blue [color=Yellow]
  GREEN = Super Flux LED blue [color=Green]
  RED = Super Flux LED blue [color=Red]
  J1 = Piezo Speaker
  R1 = Resistor [tolerance=±5% resistance=220 package="2010 [SMD]"]
  R2 = Resistor [tolerance=±5% resistance=220 package="2010 [SMD]"]
  R3 = Resistor [tolerance=±5% resistance=220 package="2010 [SMD]"]
  U1 = Mini-USB _B_ connector with 5th pin broken out. [package=usb-minib]
  J2 = female pin header, 5 pins [form="♀ (female)"]
  LCD1 = LCD screen
  R4 = Trimmer Potentiometer [maximum_resistance=10kΩ package=THT]
  Arduino_ProMini = Arduino Pro Mini (3.3V)

nets:
  GND: Q1.E, Q2.E, Q3.E, Q4.E, C1.-, U1.MTN2, U1.MTN3, U1.MTN1, U1.MTN4, U1.GND, J2.pin2, J2.pin5, LCD1.VSS, LCD1.R/W, LCD1.LED-, R4.leg1, Arduino_ProMini.GND
  N1: Q1.B, Arduino_ProMini.D10
  N2: Q1.C, RED.cathode
  N3: Q2.B, Arduino_ProMini.MOSI
  N4: Q2.C, YELLOW.cathode
  N5: Q3.B, Arduino_ProMini.MISO
  N6: Q3.C, GREEN.cathode
  N7: Q4.B, Arduino_ProMini.SCK
  N8: Q4.C, J1.pin1
  N9: C1.+, J1.pin2, J2.pin1, R4.leg2, Arduino_ProMini.VCC
  N10: YELLOW.anode, R2.Pin_0
  N11: GREEN.anode, R1.Pin_0
  N12: RED.anode, R3.Pin_0
  N13: R1.Pin_1, R2.Pin_1, R3.Pin_1, U1.VBUS, LCD1.VDD, Arduino_ProMini.RAW
  N14: J2.pin3, Arduino_ProMini.A5
  N15: J2.pin4, Arduino_ProMini.A4
  N16: LCD1.V0, R4.wiper
  N17: LCD1.RS, Arduino_ProMini.D2
  N18: LCD1.E, Arduino_ProMini.D3
  N19: LCD1.DB3, Arduino_ProMini.D4
  N20: LCD1.DB4, Arduino_ProMini.D5
  N21: LCD1.DB5, Arduino_ProMini.D6
  N22: LCD1.DB6, Arduino_ProMini.D7
  N23: LCD1.DB7, Arduino_ProMini.D8
  N24: LCD1.LED+, Arduino_ProMini.D9
